# Fritzing sketch ArduinoFirmata (saved by Fritzing 0.7.7b)
breadboards: 1

parts:
  Arduino1 = Arduino
  T1 = LM35 Temperature Sensor [package="TO92 [THT]"]
  LED1 = LED - 5mm [color="Red (635nm)" current=30mA package="5 mm [THT]"]
  R1 = Resistor [tolerance=±5% resistance=120 package=THT]

nets:
  GND: Arduino1.GND, T1.GND, R1.Pin_1
  N1: Arduino1.D3, LED1.anode
  N2: Arduino1.+5V, T1.+Vs
  N3: Arduino1.A0, T1.Vout
  N4: LED1.cathode, R1.Pin_0
